// Digital circuit 3bit_ring_counter.dig as structural Verilog
module _3bit_ring_counter (
  input  CLK,
  input  ORI,
  output [2:0] Q
);

  wire Q0, Q1, Q2;
  wire [2:0] register_1_q, register_2_q, register_3_q;

  D_FF_AS d_ff_as_1 (.Set(ORI), .D(Q2), .C(CLK), .Clr(ORI), .Q(Q0));  // open: nQ
  D_FF_AS d_ff_as_2 (.Set(1'b0), .D(Q0), .C(CLK), .Clr(ORI), .Q(Q1));  // open: nQ
  D_FF_AS d_ff_as_3 (.Set(1'b0), .D(Q1), .C(CLK), .Clr(ORI), .Q(Q2));  // open: nQ
  Register #(.Bits(3)) register_1 (.D(3'b000), .C(CLK), .en(1'b1), .Q(register_1_q));
  Register #(.Bits(3)) register_2 (.D(3'b001), .C(CLK), .en(1'b1), .Q(register_2_q));
  Register #(.Bits(3)) register_3 (.D(3'b010), .C(CLK), .en(1'b1), .Q(register_3_q));
  assign Q = Q0 ? register_1_q : 3'bz;  // Driver driver_1
  assign Q = Q1 ? register_2_q : 3'bz;  // Driver driver_2
  assign Q = Q2 ? register_3_q : 3'bz;  // Driver driver_3
endmodule
