// Digital circuit 4bit_ring_counter.dig as structural Verilog
module _4bit_ring_counter (
  input  clk
);

  wire ORI, Q0, Q1, Q2, Q3;
  wire [3:0] driver_1_out, register_1_q, register_2_q, register_3_q, register_4_q;

  Button start (.out(ORI));
  JK_FF_AS jk_ff_as_1 (.Set(ORI), .J(Q3), .C(clk), .K(1'b1), .Clr(1'b0), .Q(Q0));  // open: nQ
  LED led_1 (.in(Q0));
  JK_FF_AS jk_ff_as_2 (.Set(1'b0), .J(Q0), .C(clk), .K(1'b1), .Clr(ORI), .Q(Q1));  // open: nQ
  LED led_2 (.in(Q1));
  Register #(.Bits(4)) register_1 (.D(4'b0001), .C(clk), .en(1'b1), .Q(register_1_q));
  Register #(.Bits(4)) register_2 (.D(4'b0010), .C(clk), .en(1'b1), .Q(register_2_q));
  Register #(.Bits(4)) register_3 (.D(4'b0011), .C(clk), .en(1'b1), .Q(register_3_q));
  Register #(.Bits(4)) register_4 (.D(4'b0100), .C(clk), .en(1'b1), .Q(register_4_q));
  JK_FF_AS jk_ff_as_3 (.Set(1'b0), .J(Q1), .C(clk), .K(1'b1), .Clr(ORI), .Q(Q2));  // open: nQ
  Seven_Seg_Hex seven_seg_hex_1 (.d(driver_1_out), .dp(1'b0));
  assign driver_1_out = Q0 ? register_1_q : 4'bz;  // Driver driver_1
  assign driver_1_out = Q1 ? register_2_q : 4'bz;  // Driver driver_2
  assign driver_1_out = Q2 ? register_3_q : 4'bz;  // Driver driver_3
  assign driver_1_out = Q3 ? register_4_q : 4'bz;  // Driver driver_4
  LED led_3 (.in(Q2));
  JK_FF_AS jk_ff_as_4 (.Set(1'b0), .J(Q2), .C(clk), .K(1'b1), .Clr(ORI), .Q(Q3));  // open: nQ
  LED led_4 (.in(Q3));
endmodule
