// Digital circuit 6bit_ring_counter.dig as structural Verilog
module _6bit_ring_counter (
  input  CLK,
  output [2:0] Q
);

  wire ORI_out, Q0, Q1, Q2, Q3, Q4, Q5;
  wire [2:0] register_1_q, register_2_q, register_3_q, register_4_q, register_5_q, register_6_q;

  Button ORI (.out(ORI_out));
  D_FF_AS d_ff_as_1 (.Set(ORI_out), .D(Q5), .C(CLK), .Clr(ORI_out), .Q(Q0));  // open: nQ
  D_FF_AS d_ff_as_2 (.Set(1'b0), .D(Q0), .C(CLK), .Clr(ORI_out), .Q(Q1));  // open: nQ
  D_FF_AS d_ff_as_3 (.Set(1'b0), .D(Q1), .C(CLK), .Clr(ORI_out), .Q(Q2));  // open: nQ
  D_FF_AS d_ff_as_4 (.Set(1'b0), .D(Q2), .C(CLK), .Clr(ORI_out), .Q(Q3));  // open: nQ
  D_FF_AS d_ff_as_5 (.Set(1'b0), .D(Q3), .C(CLK), .Clr(ORI_out), .Q(Q4));  // open: nQ
  D_FF_AS d_ff_as_6 (.Set(1'b0), .D(Q4), .C(CLK), .Clr(ORI_out), .Q(Q5));  // open: nQ
  Register #(.Bits(3)) register_1 (.D(3'b000), .C(CLK), .en(1'b1), .Q(register_1_q));
  Register #(.Bits(3)) register_2 (.D(3'b001), .C(CLK), .en(1'b1), .Q(register_2_q));
  Register #(.Bits(3)) register_3 (.D(3'b010), .C(CLK), .en(1'b1), .Q(register_3_q));
  Register #(.Bits(3)) register_4 (.D(3'b011), .C(CLK), .en(1'b1), .Q(register_4_q));
  Register #(.Bits(3)) register_5 (.D(3'b100), .C(CLK), .en(1'b1), .Q(register_5_q));
  Register #(.Bits(3)) register_6 (.D(3'b101), .C(CLK), .en(1'b1), .Q(register_6_q));
  assign Q = Q0 ? register_1_q : 3'bz;  // Driver driver_1
  assign Q = Q1 ? register_2_q : 3'bz;  // Driver driver_2
  assign Q = Q2 ? register_3_q : 3'bz;  // Driver driver_3
  assign Q = Q3 ? register_4_q : 3'bz;  // Driver driver_4
  assign Q = Q4 ? register_5_q : 3'bz;  // Driver driver_5
  assign Q = Q5 ? register_6_q : 3'bz;  // Driver driver_6
endmodule
