// Digital circuit 8bit_cpu.dig as structural Verilog
module _8bit_cpu (
  input  CLK,
  output [7:0] out_2
);

  wire AC_en, IR_en, LSB_en, MAR_en, N_en, ORI_out, T6;
  wire [2:0] IR_q;
  wire [7:0] _8bit_adder_subtractor_1_s, _8bit_alu_1_ac, _8bit_alu_1_mq, AC, driver_1_out, driver_2_out, MQ,
       N_q, PC_q;
  wire [7:3] IR_q_2;

  _8bit_adder_subtractor _8bit_adder_subtractor_1 (
    .CTR(1'b0), .A(PC_q), .B(8'h1), .S(_8bit_adder_subtractor_1_s));  // open: _2
  assign driver_1_out = IR_en ? _8bit_adder_subtractor_1_s : 8'bz;  // Driver driver_1
  Register #(.Bits(8)) PC (.D(driver_1_out), .C(CLK), .en(IR_en), .Q(PC_q));
  Button ORI (.out(ORI_out));
  assign driver_2_out = MAR_en ? PC_q : 8'bz;  // Driver driver_2
  D_FF_AS d_ff_as_1 (.Set(ORI_out), .D(T6), .C(CLK), .Clr(ORI_out), .Q(MAR_en));  // open: nQ
  D_FF_AS d_ff_as_2 (.Set(1'b0), .D(MAR_en), .C(CLK), .Clr(ORI_out), .Q(IR_en));  // open: nQ
  Register #(.Bits(8)) MAR (.D(driver_2_out), .C(CLK), .en(MAR_en), .Q(out_2));
  Register #(.Bits(8)) u_AC (.D(driver_2_out), .C(CLK), .en(AC_en), .Q(AC));
  Register #(.Bits(8)) N (.D(driver_2_out), .C(CLK), .en(N_en), .Q(N_q));
  Register #(.Bits(8)) IR (.D(driver_2_out), .C(CLK), .en(IR_en), .Q({IR_q_2, IR_q}));
  Register #(.Bits(8)) u_MQ (.D(driver_2_out), .C(CLK), .en(LSB_en), .Q(MQ));
  D_FF_AS d_ff_as_3 (.Set(1'b0), .D(IR_en), .C(CLK), .Clr(ORI_out), .Q(N_en));  // open: nQ
  D_FF_AS d_ff_as_4 (.Set(1'b0), .D(N_en), .C(CLK), .Clr(ORI_out), .Q(LSB_en));  // open: nQ
  ROM #(.AddrBits(8), .Bits(8)) INSTRUCTIONS (.A(out_2), .sel(IR_en), .D(driver_2_out));
  ROM #(.AddrBits(8), .Bits(8)) OPERANDS (.A(out_2), .sel(N_en), .D(driver_2_out));
  _8bit_alu _8bit_alu_1 (.A(AC), .B(N_q), .OP(IR_q), .AC(_8bit_alu_1_ac), .MQ(_8bit_alu_1_mq));
  assign driver_2_out = AC_en ? _8bit_alu_1_ac : 8'bz;  // Driver driver_3
  assign driver_2_out = LSB_en ? _8bit_alu_1_mq : 8'bz;  // Driver driver_4
  LED led_1 (.in(MQ[7]));
  LED led_2 (.in(MQ[6]));
  D_FF_AS d_ff_as_5 (.Set(1'b0), .D(LSB_en), .C(CLK), .Clr(ORI_out), .Q(AC_en));  // open: nQ
  LED led_3 (.in(MQ[5]));
  LED led_4 (.in(MQ[4]));
  D_FF_AS d_ff_as_6 (.Set(1'b0), .D(AC_en), .C(CLK), .Clr(ORI_out), .Q(T6));  // open: nQ
  Seven_Seg_Hex seven_seg_hex_1 (.d(MQ[7:4]), .dp(1'b0));
  LED led_5 (.in(MQ[3]));
  LED led_6 (.in(MQ[2]));
  Seven_Seg_Hex seven_seg_hex_2 (.d(MQ[3:0]), .dp(1'b0));
  LED led_7 (.in(MQ[1]));
  LED led_8 (.in(MQ[0]));
  Seven_Seg_Hex seven_seg_hex_3 (.d(AC[7:4]), .dp(1'b0));
  LED led_9 (.in(AC[7]));
  LED led_10 (.in(AC[6]));
  LED led_11 (.in(AC[5]));
  LED led_12 (.in(AC[4]));
  Seven_Seg_Hex seven_seg_hex_4 (.d(AC[3:0]), .dp(1'b0));
  LED led_13 (.in(AC[3]));
  LED led_14 (.in(AC[2]));
  LED led_15 (.in(AC[1]));
  LED led_16 (.in(AC[0]));

  // Other names for the same wires on the sheet: PC_en = MAR_en; T1 = MAR_en; PC_inc = IR_en; ROM_IR = IR_en;
  //   T2 = IR_en; ROM_N = N_en; T3 = N_en; MQ_en = LSB_en; T4 = LSB_en; ALU_en = AC_en; T5 = AC_en

  // Notes on the sheet:
  //   CLK: Hz: 5
  //   contents of INSTRUCTIONS (hex, n*v repeats v):
  //   0,1,2,3,0,5,4,6,7,2
  //   contents of OPERANDS (hex, n*v repeats v):
  //   6,1,4,2,80,0,0,ff,40,a
  //   FETCH:
  //   T1: MAR <- PC
  //   T2: REG R <- ROM IR, PC <- PC + 1
  //   T3: REG N <- ROM OP
  //   EXECUÇÃO:
  //   T4: REG MQ <- ALU LSB
  //   T5: REG AC <- ALU MSB
endmodule
