// Digital circuit 8bit_divider.dig as structural Verilog
module _8bit_divider (
  input  [7:0] A,
  input  [7:0] B,
  output [7:0] R,
  output [7:0] Q
);

  wire _8bit_adder_subtractor_1__2, _8bit_adder_subtractor_2__2, _8bit_adder_subtractor_3__2,
       _8bit_adder_subtractor_4__2, _8bit_adder_subtractor_5__2, _8bit_adder_subtractor_6__2,
       _8bit_adder_subtractor_7__2, _8bit_adder_subtractor_8__2;
  wire [1:1] multiplexer_1_out;
  wire [7:0] _8bit_adder_subtractor_1_s, _8bit_adder_subtractor_2_s, _8bit_adder_subtractor_3_s,
       _8bit_adder_subtractor_4_s, _8bit_adder_subtractor_5_s, _8bit_adder_subtractor_6_s,
       _8bit_adder_subtractor_7_s, _8bit_adder_subtractor_8_s, multiplexer_2_out, multiplexer_3_out,
       multiplexer_4_out, multiplexer_5_out, multiplexer_6_out, multiplexer_7_out;
  wire [7:1] multiplexer_1_out_2;

  _8bit_adder_subtractor _8bit_adder_subtractor_1 (
    .CTR(1'b1), .A({{7{1'b0}}, A[7]}), .B(B), .S(_8bit_adder_subtractor_1_s), ._2(_8bit_adder_subtractor_1__2));
  Multiplexer #(.Bits(8)) multiplexer_1 (
    .sel(_8bit_adder_subtractor_1__2), .in_0(_8bit_adder_subtractor_1_s), .in_1({{7{1'b0}}, A[7]}),
    .out({multiplexer_1_out_2, multiplexer_1_out[1]}));
  _8bit_adder_subtractor _8bit_adder_subtractor_2 (
    .CTR(1'b1), .A({{6{1'b0}}, multiplexer_1_out[1], A[6]}), .B(B), .S(_8bit_adder_subtractor_2_s),
    ._2(_8bit_adder_subtractor_2__2));
  Multiplexer #(.Bits(8)) multiplexer_2 (
    .sel(_8bit_adder_subtractor_2__2), .in_0(_8bit_adder_subtractor_2_s),
    .in_1({{6{1'b0}}, multiplexer_1_out[1], A[6]}), .out(multiplexer_2_out));
  _8bit_adder_subtractor _8bit_adder_subtractor_3 (
    .CTR(1'b1), .A({{5{1'b0}}, multiplexer_2_out[1:0], A[5]}), .B(B), .S(_8bit_adder_subtractor_3_s),
    ._2(_8bit_adder_subtractor_3__2));
  Multiplexer #(.Bits(8)) multiplexer_3 (
    .sel(_8bit_adder_subtractor_3__2), .in_0(_8bit_adder_subtractor_3_s),
    .in_1({{5{1'b0}}, multiplexer_2_out[1:0], A[5]}), .out(multiplexer_3_out));
  _8bit_adder_subtractor _8bit_adder_subtractor_4 (
    .CTR(1'b1), .A({4'b0000, multiplexer_3_out[2:0], A[4]}), .B(B), .S(_8bit_adder_subtractor_4_s),
    ._2(_8bit_adder_subtractor_4__2));
  Multiplexer #(.Bits(8)) multiplexer_4 (
    .sel(_8bit_adder_subtractor_4__2), .in_0(_8bit_adder_subtractor_4_s),
    .in_1({4'b0000, multiplexer_3_out[2:0], A[4]}), .out(multiplexer_4_out));
  _8bit_adder_subtractor _8bit_adder_subtractor_5 (
    .CTR(1'b1), .A({3'b000, multiplexer_4_out[3:0], A[3]}), .B(B), .S(_8bit_adder_subtractor_5_s),
    ._2(_8bit_adder_subtractor_5__2));
  Multiplexer #(.Bits(8)) multiplexer_5 (
    .sel(_8bit_adder_subtractor_5__2), .in_0(_8bit_adder_subtractor_5_s),
    .in_1({3'b000, multiplexer_4_out[3:0], A[3]}), .out(multiplexer_5_out));
  _8bit_adder_subtractor _8bit_adder_subtractor_6 (
    .CTR(1'b1), .A({2'b00, multiplexer_5_out[4:0], A[2]}), .B(B), .S(_8bit_adder_subtractor_6_s),
    ._2(_8bit_adder_subtractor_6__2));
  Multiplexer #(.Bits(8)) multiplexer_6 (
    .sel(_8bit_adder_subtractor_6__2), .in_0(_8bit_adder_subtractor_6_s),
    .in_1({2'b00, multiplexer_5_out[4:0], A[2]}), .out(multiplexer_6_out));
  _8bit_adder_subtractor _8bit_adder_subtractor_7 (
    .CTR(1'b1), .A({1'b0, multiplexer_6_out[5:0], A[1]}), .B(B), .S(_8bit_adder_subtractor_7_s),
    ._2(_8bit_adder_subtractor_7__2));
  Multiplexer #(.Bits(8)) multiplexer_7 (
    .sel(_8bit_adder_subtractor_7__2), .in_0(_8bit_adder_subtractor_7_s),
    .in_1({1'b0, multiplexer_6_out[5:0], A[1]}), .out(multiplexer_7_out));
  _8bit_adder_subtractor _8bit_adder_subtractor_8 (
    .CTR(1'b1), .A({multiplexer_7_out[6:0], A[0]}), .B(B), .S(_8bit_adder_subtractor_8_s),
    ._2(_8bit_adder_subtractor_8__2));
  Multiplexer #(.Bits(8)) multiplexer_8 (
    .sel(_8bit_adder_subtractor_8__2), .in_0(_8bit_adder_subtractor_8_s),
    .in_1({multiplexer_7_out[6:0], A[0]}), .out(R));
  not not_1 (Q[0], _8bit_adder_subtractor_8__2);
  not not_2 (Q[1], _8bit_adder_subtractor_7__2);
  not not_3 (Q[2], _8bit_adder_subtractor_6__2);
  not not_4 (Q[3], _8bit_adder_subtractor_5__2);
  not not_5 (Q[4], _8bit_adder_subtractor_4__2);
  not not_6 (Q[5], _8bit_adder_subtractor_3__2);
  not not_7 (Q[6], _8bit_adder_subtractor_2__2);
  not not_8 (Q[7], _8bit_adder_subtractor_1__2);
endmodule
