// Digital circuit 8bit_multiplier.dig as structural Verilog
module _8bit_multiplier (
  input  [7:0] A,
  input  [7:0] B,
  output [15:0] P
);

  wire and_2_out, and_3_out, and_4_out, and_5_out, and_6_out, and_7_out, and_8_out, and_9_out, and_10_out,
       and_11_out, and_12_out, and_13_out, and_14_out, and_15_out, and_16_out, and_17_out, and_18_out,
       and_19_out, and_20_out, and_21_out, and_22_out, and_23_out, and_24_out, and_25_out, and_26_out,
       and_27_out, and_28_out, and_29_out, and_30_out, and_31_out, and_32_out, and_33_out, and_34_out,
       and_35_out, and_36_out, and_37_out, and_38_out, and_39_out, and_40_out, and_41_out, and_42_out,
       and_43_out, and_44_out, and_45_out, and_46_out, and_47_out, and_48_out, and_49_out, and_50_out,
       and_51_out, and_52_out, and_53_out, and_54_out, and_55_out, and_56_out, and_57_out, and_58_out,
       and_59_out, and_60_out, and_61_out, and_62_out, and_63_out, and_64_out, full_adder_1_cout,
       full_adder_1_s, full_adder_2_cout, full_adder_2_s, full_adder_3_cout, full_adder_3_s,
       full_adder_4_cout, full_adder_4_s, full_adder_5_cout, full_adder_5_s, full_adder_6_cout,
       full_adder_6_s, full_adder_7_cout, full_adder_7_s, full_adder_8_cout, full_adder_8_s,
       full_adder_9_cout, full_adder_9_s, full_adder_10_cout, full_adder_10_s, full_adder_11_cout,
       full_adder_11_s, full_adder_12_cout, full_adder_12_s, full_adder_13_cout, full_adder_13_s,
       full_adder_14_cout, full_adder_14_s, full_adder_15_cout, full_adder_15_s, full_adder_16_cout,
       full_adder_16_s, full_adder_17_cout, full_adder_17_s, full_adder_18_cout, full_adder_18_s,
       full_adder_19_cout, full_adder_19_s, full_adder_20_cout, full_adder_20_s, full_adder_21_cout,
       full_adder_21_s, full_adder_22_cout, full_adder_22_s, full_adder_23_cout, full_adder_23_s,
       full_adder_24_cout, full_adder_24_s, full_adder_25_cout, full_adder_25_s, full_adder_26_cout,
       full_adder_26_s, full_adder_27_cout, full_adder_27_s, full_adder_28_cout, full_adder_28_s,
       full_adder_29_cout, full_adder_29_s, full_adder_30_cout, full_adder_30_s, full_adder_31_cout,
       full_adder_31_s, full_adder_32_cout, full_adder_32_s, full_adder_33_cout, full_adder_33_s,
       full_adder_34_cout, full_adder_34_s, full_adder_35_cout, full_adder_35_s, full_adder_36_cout,
       full_adder_36_s, full_adder_37_cout, full_adder_37_s, full_adder_38_cout, full_adder_38_s,
       full_adder_39_cout, full_adder_39_s, full_adder_40_cout, full_adder_40_s, full_adder_41_cout,
       full_adder_41_s, full_adder_42_cout, full_adder_43_cout, full_adder_44_cout, full_adder_45_cout,
       full_adder_46_cout, full_adder_47_cout, half_adder_1_c, half_adder_2_c, half_adder_2_s,
       half_adder_3_c, half_adder_4_c, half_adder_5_c, half_adder_6_c, half_adder_7_c, half_adder_8_c;

  and and_1 (P[0], B[0], A[0]);
  and and_2 (and_2_out, B[0], A[1]);
  and and_3 (and_3_out, B[0], A[2]);
  and and_4 (and_4_out, B[0], A[3]);
  and and_5 (and_5_out, B[0], A[4]);
  and and_6 (and_6_out, B[0], A[5]);
  and and_7 (and_7_out, B[0], A[6]);
  and and_8 (and_8_out, B[0], A[7]);
  and and_9 (and_9_out, B[1], A[0]);
  and and_10 (and_10_out, B[1], A[1]);
  and and_11 (and_11_out, B[1], A[2]);
  and and_12 (and_12_out, B[1], A[3]);
  and and_13 (and_13_out, B[1], A[4]);
  and and_14 (and_14_out, B[1], A[5]);
  and and_15 (and_15_out, B[1], A[6]);
  and and_16 (and_16_out, B[1], A[7]);
  half_adder half_adder_1 (.A(and_9_out), .B(and_2_out), .S(P[1]), .C(half_adder_1_c));
  full_adder full_adder_1 (
    .A(half_adder_1_c), .B(and_10_out), .Cin(and_3_out), .S(full_adder_1_s), .Cout(full_adder_1_cout));
  full_adder full_adder_2 (
    .A(full_adder_1_cout), .B(and_11_out), .Cin(and_4_out), .S(full_adder_2_s), .Cout(full_adder_2_cout));
  full_adder full_adder_3 (
    .A(full_adder_2_cout), .B(and_12_out), .Cin(and_5_out), .S(full_adder_3_s), .Cout(full_adder_3_cout));
  full_adder full_adder_4 (
    .A(full_adder_3_cout), .B(and_13_out), .Cin(and_6_out), .S(full_adder_4_s), .Cout(full_adder_4_cout));
  full_adder full_adder_5 (
    .A(full_adder_4_cout), .B(and_14_out), .Cin(and_7_out), .S(full_adder_5_s), .Cout(full_adder_5_cout));
  full_adder full_adder_6 (
    .A(full_adder_5_cout), .B(and_15_out), .Cin(and_8_out), .S(full_adder_6_s), .Cout(full_adder_6_cout));
  half_adder half_adder_2 (.A(full_adder_6_cout), .B(and_16_out), .S(half_adder_2_s), .C(half_adder_2_c));
  and and_17 (and_17_out, B[2], A[0]);
  and and_18 (and_18_out, B[2], A[1]);
  and and_19 (and_19_out, B[2], A[2]);
  and and_20 (and_20_out, B[2], A[3]);
  and and_21 (and_21_out, B[2], A[4]);
  and and_22 (and_22_out, B[2], A[5]);
  and and_23 (and_23_out, B[2], A[6]);
  and and_24 (and_24_out, B[2], A[7]);
  half_adder half_adder_3 (.A(and_17_out), .B(full_adder_1_s), .S(P[2]), .C(half_adder_3_c));
  full_adder full_adder_7 (
    .A(half_adder_3_c), .B(and_18_out), .Cin(full_adder_2_s), .S(full_adder_7_s), .Cout(full_adder_7_cout));
  full_adder full_adder_8 (
    .A(full_adder_7_cout), .B(and_19_out), .Cin(full_adder_3_s), .S(full_adder_8_s), .Cout(full_adder_8_cout));
  full_adder full_adder_9 (
    .A(full_adder_8_cout), .B(and_20_out), .Cin(full_adder_4_s), .S(full_adder_9_s), .Cout(full_adder_9_cout));
  full_adder full_adder_10 (
    .A(full_adder_9_cout), .B(and_21_out), .Cin(full_adder_5_s), .S(full_adder_10_s),
    .Cout(full_adder_10_cout));
  full_adder full_adder_11 (
    .A(full_adder_10_cout), .B(and_22_out), .Cin(full_adder_6_s), .S(full_adder_11_s),
    .Cout(full_adder_11_cout));
  full_adder full_adder_12 (
    .A(full_adder_11_cout), .B(and_23_out), .Cin(half_adder_2_s), .S(full_adder_12_s),
    .Cout(full_adder_12_cout));
  full_adder full_adder_13 (
    .A(full_adder_12_cout), .B(and_24_out), .Cin(half_adder_2_c), .S(full_adder_13_s),
    .Cout(full_adder_13_cout));
  and and_25 (and_25_out, B[3], A[0]);
  and and_26 (and_26_out, B[3], A[1]);
  and and_27 (and_27_out, B[3], A[2]);
  and and_28 (and_28_out, B[3], A[3]);
  and and_29 (and_29_out, B[3], A[4]);
  and and_30 (and_30_out, B[3], A[5]);
  and and_31 (and_31_out, B[3], A[6]);
  and and_32 (and_32_out, B[3], A[7]);
  half_adder half_adder_4 (.A(and_25_out), .B(full_adder_7_s), .S(P[3]), .C(half_adder_4_c));
  full_adder full_adder_14 (
    .A(half_adder_4_c), .B(and_26_out), .Cin(full_adder_8_s), .S(full_adder_14_s), .Cout(full_adder_14_cout));
  full_adder full_adder_15 (
    .A(full_adder_14_cout), .B(and_27_out), .Cin(full_adder_9_s), .S(full_adder_15_s),
    .Cout(full_adder_15_cout));
  full_adder full_adder_16 (
    .A(full_adder_15_cout), .B(and_28_out), .Cin(full_adder_10_s), .S(full_adder_16_s),
    .Cout(full_adder_16_cout));
  full_adder full_adder_17 (
    .A(full_adder_16_cout), .B(and_29_out), .Cin(full_adder_11_s), .S(full_adder_17_s),
    .Cout(full_adder_17_cout));
  full_adder full_adder_18 (
    .A(full_adder_17_cout), .B(and_30_out), .Cin(full_adder_12_s), .S(full_adder_18_s),
    .Cout(full_adder_18_cout));
  full_adder full_adder_19 (
    .A(full_adder_18_cout), .B(and_31_out), .Cin(full_adder_13_s), .S(full_adder_19_s),
    .Cout(full_adder_19_cout));
  full_adder full_adder_20 (
    .A(full_adder_19_cout), .B(and_32_out), .Cin(full_adder_13_cout), .S(full_adder_20_s),
    .Cout(full_adder_20_cout));
  and and_33 (and_33_out, B[4], A[0]);
  and and_34 (and_34_out, B[4], A[1]);
  and and_35 (and_35_out, B[4], A[2]);
  and and_36 (and_36_out, B[4], A[3]);
  and and_37 (and_37_out, B[4], A[4]);
  and and_38 (and_38_out, B[4], A[5]);
  and and_39 (and_39_out, B[4], A[6]);
  and and_40 (and_40_out, B[4], A[7]);
  half_adder half_adder_5 (.A(and_33_out), .B(full_adder_14_s), .S(P[4]), .C(half_adder_5_c));
  full_adder full_adder_21 (
    .A(half_adder_5_c), .B(and_34_out), .Cin(full_adder_15_s), .S(full_adder_21_s), .Cout(full_adder_21_cout));
  full_adder full_adder_22 (
    .A(full_adder_21_cout), .B(and_35_out), .Cin(full_adder_16_s), .S(full_adder_22_s),
    .Cout(full_adder_22_cout));
  full_adder full_adder_23 (
    .A(full_adder_22_cout), .B(and_36_out), .Cin(full_adder_17_s), .S(full_adder_23_s),
    .Cout(full_adder_23_cout));
  full_adder full_adder_24 (
    .A(full_adder_23_cout), .B(and_37_out), .Cin(full_adder_18_s), .S(full_adder_24_s),
    .Cout(full_adder_24_cout));
  full_adder full_adder_25 (
    .A(full_adder_24_cout), .B(and_38_out), .Cin(full_adder_19_s), .S(full_adder_25_s),
    .Cout(full_adder_25_cout));
  full_adder full_adder_26 (
    .A(full_adder_25_cout), .B(and_39_out), .Cin(full_adder_20_s), .S(full_adder_26_s),
    .Cout(full_adder_26_cout));
  full_adder full_adder_27 (
    .A(full_adder_26_cout), .B(and_40_out), .Cin(full_adder_20_cout), .S(full_adder_27_s),
    .Cout(full_adder_27_cout));
  and and_41 (and_41_out, B[5], A[0]);
  and and_42 (and_42_out, B[5], A[1]);
  and and_43 (and_43_out, B[5], A[2]);
  and and_44 (and_44_out, B[5], A[3]);
  and and_45 (and_45_out, B[5], A[4]);
  and and_46 (and_46_out, B[5], A[5]);
  and and_47 (and_47_out, B[5], A[6]);
  and and_48 (and_48_out, B[5], A[7]);
  half_adder half_adder_6 (.A(and_41_out), .B(full_adder_21_s), .S(P[5]), .C(half_adder_6_c));
  full_adder full_adder_28 (
    .A(half_adder_6_c), .B(and_42_out), .Cin(full_adder_22_s), .S(full_adder_28_s), .Cout(full_adder_28_cout));
  full_adder full_adder_29 (
    .A(full_adder_28_cout), .B(and_43_out), .Cin(full_adder_23_s), .S(full_adder_29_s),
    .Cout(full_adder_29_cout));
  full_adder full_adder_30 (
    .A(full_adder_29_cout), .B(and_44_out), .Cin(full_adder_24_s), .S(full_adder_30_s),
    .Cout(full_adder_30_cout));
  full_adder full_adder_31 (
    .A(full_adder_30_cout), .B(and_45_out), .Cin(full_adder_25_s), .S(full_adder_31_s),
    .Cout(full_adder_31_cout));
  full_adder full_adder_32 (
    .A(full_adder_31_cout), .B(and_46_out), .Cin(full_adder_26_s), .S(full_adder_32_s),
    .Cout(full_adder_32_cout));
  full_adder full_adder_33 (
    .A(full_adder_32_cout), .B(and_47_out), .Cin(full_adder_27_s), .S(full_adder_33_s),
    .Cout(full_adder_33_cout));
  full_adder full_adder_34 (
    .A(full_adder_33_cout), .B(and_48_out), .Cin(full_adder_27_cout), .S(full_adder_34_s),
    .Cout(full_adder_34_cout));
  and and_49 (and_49_out, B[6], A[0]);
  and and_50 (and_50_out, B[6], A[1]);
  and and_51 (and_51_out, B[6], A[2]);
  and and_52 (and_52_out, B[6], A[3]);
  and and_53 (and_53_out, B[6], A[4]);
  and and_54 (and_54_out, B[6], A[5]);
  and and_55 (and_55_out, B[6], A[6]);
  and and_56 (and_56_out, B[6], A[7]);
  half_adder half_adder_7 (.A(and_49_out), .B(full_adder_28_s), .S(P[6]), .C(half_adder_7_c));
  full_adder full_adder_35 (
    .A(half_adder_7_c), .B(and_50_out), .Cin(full_adder_29_s), .S(full_adder_35_s), .Cout(full_adder_35_cout));
  full_adder full_adder_36 (
    .A(full_adder_35_cout), .B(and_51_out), .Cin(full_adder_30_s), .S(full_adder_36_s),
    .Cout(full_adder_36_cout));
  full_adder full_adder_37 (
    .A(full_adder_36_cout), .B(and_52_out), .Cin(full_adder_31_s), .S(full_adder_37_s),
    .Cout(full_adder_37_cout));
  full_adder full_adder_38 (
    .A(full_adder_37_cout), .B(and_53_out), .Cin(full_adder_32_s), .S(full_adder_38_s),
    .Cout(full_adder_38_cout));
  full_adder full_adder_39 (
    .A(full_adder_38_cout), .B(and_54_out), .Cin(full_adder_33_s), .S(full_adder_39_s),
    .Cout(full_adder_39_cout));
  full_adder full_adder_40 (
    .A(full_adder_39_cout), .B(and_55_out), .Cin(full_adder_34_s), .S(full_adder_40_s),
    .Cout(full_adder_40_cout));
  full_adder full_adder_41 (
    .A(full_adder_40_cout), .B(and_56_out), .Cin(full_adder_34_cout), .S(full_adder_41_s),
    .Cout(full_adder_41_cout));
  and and_57 (and_57_out, B[7], A[0]);
  and and_58 (and_58_out, B[7], A[1]);
  and and_59 (and_59_out, B[7], A[2]);
  and and_60 (and_60_out, B[7], A[3]);
  and and_61 (and_61_out, B[7], A[4]);
  and and_62 (and_62_out, B[7], A[5]);
  and and_63 (and_63_out, B[7], A[6]);
  and and_64 (and_64_out, B[7], A[7]);
  half_adder half_adder_8 (.A(and_57_out), .B(full_adder_35_s), .S(P[7]), .C(half_adder_8_c));
  full_adder full_adder_42 (
    .A(half_adder_8_c), .B(and_58_out), .Cin(full_adder_36_s), .S(P[8]), .Cout(full_adder_42_cout));
  full_adder full_adder_43 (
    .A(full_adder_42_cout), .B(and_59_out), .Cin(full_adder_37_s), .S(P[9]), .Cout(full_adder_43_cout));
  full_adder full_adder_44 (
    .A(full_adder_43_cout), .B(and_60_out), .Cin(full_adder_38_s), .S(P[10]), .Cout(full_adder_44_cout));
  full_adder full_adder_45 (
    .A(full_adder_44_cout), .B(and_61_out), .Cin(full_adder_39_s), .S(P[11]), .Cout(full_adder_45_cout));
  full_adder full_adder_46 (
    .A(full_adder_45_cout), .B(and_62_out), .Cin(full_adder_40_s), .S(P[12]), .Cout(full_adder_46_cout));
  full_adder full_adder_47 (
    .A(full_adder_46_cout), .B(and_63_out), .Cin(full_adder_41_s), .S(P[13]), .Cout(full_adder_47_cout));
  full_adder full_adder_48 (.A(full_adder_47_cout), .B(and_64_out), .Cin(full_adder_41_cout), .S(P[14]), .Cout(P[15]));
endmodule
