// Digital circuit fetch.dig as structural Verilog
module fetch (
  input  clk,
  input  in_3,
  input  in_4,
  output [7:0] out_2
);

  wire [7:0] _8bit_adder_subtractor_1_s, PC_q;

  Register #(.Bits(8)) PC (.D(_8bit_adder_subtractor_1_s), .C(clk), .en(in_3), .Q(PC_q));
  ROM #(.AddrBits(8), .Bits(8)) rom_1 (.A(PC_q), .sel(in_4), .D(out_2));
  _8bit_adder_subtractor _8bit_adder_subtractor_1 (
    .CTR(1'b0), .A(PC_q), .B(8'h1), .S(_8bit_adder_subtractor_1_s));  // open: _2

  // Notes on the sheet:
  //   contents of rom_1 (hex, n*v repeats v):
  //   1,3,2
endmodule
